# Fritzing sketch DS18B20 (saved by Fritzing 0.9.3b)

parts:
  Grove1 = Grove-DS18B20
  Composant1 = Base Shield V2

nets:
  N1: Grove1.SIG, Composant1.pin_99
  N2: Grove1.NC, Composant1.pin_98
  N3: Grove1.VCC, Composant1.pin_97
  N4: Grove1.GND, Composant1.pin_96
